// Logisim project lab2_prob2.circ as structural Verilog: 1 circuit, main circuit main
module main (
  input  Front_Car,
  input  Car_1,
  input  Car_2,
  input  Car_3,
  input  Car_4,
  input  Car_5,
  input  Car_6
);

  wire A_out, and_1_out, and_2_out, and_3_out, and_4_out, and_5_out, and_6_out, and_7_out, B_out, C_out,
       D_out, E_out, F_out, G_out, not_1_out, not_2_out, not_3_out, not_4_out, not_5_out, not_6_out,
       not_7_out, not_8_out, not_9_out, or_1_out, or_2_out, or_3_out;

  or or_1 (or_1_out, Car_1, Car_4, Car_5);
  or or_2 (or_2_out, Car_2, Car_4, Car_6);
  or or_3 (or_3_out, Car_3, Car_5, Car_6);
  not not_1 (not_1_out, or_2_out);
  not not_2 (not_2_out, or_3_out);
  not not_3 (not_3_out, or_1_out);
  not not_4 (not_4_out, or_3_out);
  not not_5 (not_5_out, or_1_out);
  not not_6 (not_6_out, or_2_out);
  not not_7 (not_7_out, or_3_out);
  not not_8 (not_8_out, or_2_out);
  not not_9 (not_9_out, or_1_out);
  buf and_1 (and_1_out, Front_Car);  // AND_Gate
  and and_2 (and_2_out, or_1_out, not_1_out, not_2_out);
  and and_3 (and_3_out, not_3_out, or_2_out, not_4_out);
  and and_4 (and_4_out, not_5_out, not_6_out, or_3_out);
  and and_5 (and_5_out, or_1_out, or_2_out, not_7_out);
  and and_6 (and_6_out, or_1_out, or_1_out, not_8_out, or_3_out);
  and and_7 (and_7_out, not_9_out, or_2_out, or_3_out);
  or A (A_out, and_1_out, and_3_out, and_7_out, and_4_out, and_6_out);
  or B (B_out, and_1_out, and_2_out, and_3_out, and_4_out, and_5_out);
  or C (C_out, and_4_out, and_5_out, and_1_out, and_6_out, and_7_out, and_2_out);
  or D (D_out, and_1_out, and_3_out, and_6_out, and_4_out, and_7_out);
  or E (E_out, and_1_out, and_3_out, and_7_out);
  or F (F_out, and_1_out, and_5_out, and_6_out, and_7_out);
  or G (G_out, and_3_out, and_4_out, and_5_out, and_6_out, and_7_out);
  _7_Segment_Display u_7_segment_display_1 (
    .g(G_out), .f(F_out), .a(A_out), .b(B_out), .e(E_out), .d(D_out), .c(C_out));  // open: dp

  // Notes on the sheet:
  //   Front Car
  //   Car 1
  //   Car 2
  //   Car 3
  //   Car 4
  //   Car 5
  //   Car 6
endmodule
