// Logisim project lab3_prob2.circ as structural Verilog: 1 circuit, main circuit main
module main (
  output out_1
);

  wire and_1_out, and_2_out, and_3_out, and_4_out, button_1_out, clock_1_out, nor_1_out, nor_2_out,
       nor_4_out, not_1_out, not_2_out, not_3_out, t_ff_1_q;

  Button button_1 (.out(button_1_out));
  Clock clock_1 (.out(clock_1_out));
  T_Flip_Flop t_ff_1 (.clk(clock_1_out), .T(button_1_out), .Q(t_ff_1_q));  // open: Qn, preset, reset, en
  not not_1 (not_1_out, t_ff_1_q);
  and and_1 (and_1_out, clock_1_out, t_ff_1_q);
  and and_2 (and_2_out, not_1_out, clock_1_out);
  not not_2 (not_2_out, clock_1_out);
  nor nor_1 (nor_1_out, and_1_out, nor_2_out);
  nor nor_2 (nor_2_out, nor_1_out, and_2_out);
  not not_3 (not_3_out, nor_1_out);
  and and_3 (and_3_out, nor_1_out, not_2_out);
  and and_4 (and_4_out, not_2_out, not_3_out);
  nor nor_3 (out_1, and_3_out, nor_4_out);
  nor nor_4 (nor_4_out, out_1, and_4_out);

  // Notes on the sheet:
  //   Stand in for the Toggle Switch.
  //   Explaination is in part 3.
endmodule
