// Logisim project lab3_prob3.circ as structural Verilog: 3 circuits, main circuit main
module main (
  input  IO_Enable
);

  wire and_1_out, and_2_out, and_3_out, and_4_out, and_5_out, and_6_out, and_7_out, button_1_out,
       button_2_out, button_3_out, button_4_out, button_5_out, button_6_out, button_7_out, clock_1_out,
       d_ff_2_1_out_2, d_ff_2_2_out_2, d_ff_2_3_out_2, d_ff_2_4_out_2, d_ff_2_5_out_2, d_ff_2_6_out_2,
       d_ff_2_7_out_2, not_1_out, not_2_out, not_3_out, not_4_out, not_5_out, not_6_out, not_7_out,
       not_8_out, not_9_out, not_10_out, not_11_out, not_12_out, not_13_out, not_14_out, not_15_out,
       not_16_out, not_17_out, not_18_out, or_1_out, or_2_out, or_3_out, or_4_out, t_ff_1_q, t_ff_2_q,
       t_ff_3_q, t_ff_4_q, t_ff_5_q, t_ff_6_q, t_ff_7_q;

  Clock clock_1 (.out(clock_1_out));
  Button button_1 (.out(button_1_out));
  Button button_2 (.out(button_2_out));
  Button button_3 (.out(button_3_out));
  Button button_4 (.out(button_4_out));
  Button button_5 (.out(button_5_out));
  Button button_6 (.out(button_6_out));
  Button button_7 (.out(button_7_out));
  or or_1 (or_1_out, button_1_out, button_5_out);
  or or_2 (or_2_out, button_2_out, button_5_out, button_6_out);
  or or_3 (or_3_out, button_3_out, button_6_out, button_7_out);
  or or_4 (or_4_out, button_4_out, button_7_out);
  not not_1 (not_1_out, or_2_out);
  not not_2 (not_2_out, or_3_out);
  not not_3 (not_3_out, or_4_out);
  not not_4 (not_4_out, or_1_out);
  not not_5 (not_5_out, or_3_out);
  not not_6 (not_6_out, or_4_out);
  not not_7 (not_7_out, or_1_out);
  not not_8 (not_8_out, or_2_out);
  not not_9 (not_9_out, or_4_out);
  and and_1 (and_1_out, or_1_out, not_1_out, IO_Enable, not_2_out, not_3_out);
  and and_2 (and_2_out, not_4_out, or_2_out, IO_Enable, not_5_out, not_6_out);
  and and_3 (and_3_out, not_7_out, not_8_out, IO_Enable, or_3_out, not_9_out);
  not not_10 (not_10_out, or_1_out);
  not not_11 (not_11_out, or_2_out);
  and and_4 (and_4_out, not_10_out, not_11_out, IO_Enable, not_12_out, or_4_out);
  not not_12 (not_12_out, or_3_out);
  and and_5 (and_5_out, or_1_out, or_2_out, IO_Enable, not_13_out, not_14_out);
  not not_13 (not_13_out, or_3_out);
  not not_14 (not_14_out, or_4_out);
  not not_15 (not_15_out, or_1_out);
  and and_6 (and_6_out, not_15_out, or_2_out, IO_Enable, or_3_out, not_16_out);
  not not_16 (not_16_out, or_4_out);
  not not_17 (not_17_out, or_1_out);
  not not_18 (not_18_out, or_2_out);
  and and_7 (and_7_out, not_17_out, not_18_out, IO_Enable, or_3_out, or_4_out);
  T_Flip_Flop t_ff_1 (.clk(clock_1_out), .T(and_1_out), .Q(t_ff_1_q));  // open: Qn, preset, reset, en
  T_Flip_Flop t_ff_2 (.clk(clock_1_out), .T(and_2_out), .Q(t_ff_2_q));  // open: Qn, preset, reset, en
  T_Flip_Flop t_ff_3 (.clk(clock_1_out), .T(and_3_out), .Q(t_ff_3_q));  // open: Qn, preset, reset, en
  T_Flip_Flop t_ff_4 (.clk(clock_1_out), .T(and_4_out), .Q(t_ff_4_q));  // open: Qn, preset, reset, en
  T_Flip_Flop t_ff_5 (.clk(clock_1_out), .T(and_5_out), .Q(t_ff_5_q));  // open: Qn, preset, reset, en
  T_Flip_Flop t_ff_6 (.clk(clock_1_out), .T(and_6_out), .Q(t_ff_6_q));  // open: Qn, preset, reset, en
  T_Flip_Flop t_ff_7 (.clk(clock_1_out), .T(and_7_out), .Q(t_ff_7_q));  // open: Qn, preset, reset, en
  D_Flip_Flop_2 d_ff_2_1 (.out_2(d_ff_2_1_out_2), .in_1(t_ff_1_q));
  D_Flip_Flop_2 d_ff_2_2 (.out_2(d_ff_2_2_out_2), .in_1(t_ff_2_q));
  D_Flip_Flop_2 d_ff_2_3 (.out_2(d_ff_2_3_out_2), .in_1(t_ff_3_q));
  D_Flip_Flop_2 d_ff_2_4 (.out_2(d_ff_2_4_out_2), .in_1(t_ff_4_q));
  D_Flip_Flop_2 d_ff_2_5 (.out_2(d_ff_2_5_out_2), .in_1(t_ff_5_q));
  D_Flip_Flop_2 d_ff_2_6 (.out_2(d_ff_2_6_out_2), .in_1(t_ff_6_q));
  D_Flip_Flop_2 d_ff_2_7 (.out_2(d_ff_2_7_out_2), .in_1(t_ff_7_q));
  LED led_1 (.in(d_ff_2_1_out_2));
  LED led_2 (.in(d_ff_2_2_out_2));
  LED led_3 (.in(d_ff_2_3_out_2));
  LED led_4 (.in(d_ff_2_4_out_2));
  LED led_5 (.in(d_ff_2_5_out_2));
  LED led_6 (.in(d_ff_2_6_out_2));
  LED led_7 (.in(d_ff_2_7_out_2));

  // Notes on the sheet:
  //   Clock
  //   Door 1
  //   Door 2
  //   Door 3
  //   Door 4
  //   A/C
  //   Engine
  //   Wipers
  //   PLEASE NOTE: These T-Flip-Flops are standing in place of 
  //   The toggle switch. This is because I have built multiple versions
  //   of a toggle switch, however, Logisim doesn't recognize the initializer. Therefore
  //   these T-Flip-Flops are stand-ins due to Logisim's inability to recognize a custom 
  //   Toggle switch or T-Flip-Flop. 
  //   In order for this segment to work correctly,
  //   Please activate the D-Flip-Flop curcuit included.
  //   PLEASE NOTE: The included toggle switch is one
  //   That the TA himself wrote. This should show Logisim's apparent 
  //   hated of these kinds of switches.
endmodule

module D_Flip_Flop_2 (
  input  in_1,
  output out_2
);

  wire and_1_out, and_2_out, and_3_out, and_4_out, clock_1_out, nor_1_out, nor_2_out, nor_4_out, not_1_out,
       not_2_out, not_3_out;

  not not_1 (not_1_out, in_1);
  Clock clock_1 (.out(clock_1_out));
  and and_1 (and_1_out, clock_1_out, in_1, in_1);
  and and_2 (and_2_out, not_1_out, clock_1_out);
  not not_2 (not_2_out, clock_1_out);
  nor nor_1 (nor_1_out, and_1_out, nor_2_out);
  nor nor_2 (nor_2_out, nor_1_out, and_2_out);
  not not_3 (not_3_out, nor_1_out);
  and and_3 (and_3_out, nor_1_out, not_2_out);
  and and_4 (and_4_out, not_2_out, not_3_out);
  nor nor_3 (out_2, and_3_out, nor_4_out);
  nor nor_4 (nor_4_out, out_2, and_4_out);
endmodule

module Toggle_Switch (
  output out_1
);

  wire and_1_out, and_2_out, and_3_out, and_4_out, and_5_out, and_6_out, and_7_out, and_8_out, button_1_out,
       clock_1_out, nor_1_out, nor_2_out, nor_4_out, not_1_out, not_2_out, not_3_out, xor_1_out;

  Button button_1 (.out(button_1_out));
  Clock clock_1 (.out(clock_1_out));
  not not_1 (not_1_out, xor_1_out);
  xor xor_1 (xor_1_out, button_1_out, out_1);
  and and_1 (and_1_out, xor_1_out, clock_1_out);
  and and_2 (and_2_out, not_1_out, clock_1_out);
  and and_3 (and_3_out, and_1_out, clock_1_out);
  and and_4 (and_4_out, and_2_out, clock_1_out);
  not not_2 (not_2_out, clock_1_out);
  nor nor_1 (nor_1_out, and_3_out, nor_2_out);
  nor nor_2 (nor_2_out, nor_1_out, and_4_out);
  not not_3 (not_3_out, nor_1_out);
  and and_5 (and_5_out, nor_1_out, not_2_out);
  and and_6 (and_6_out, not_3_out, not_2_out);
  and and_7 (and_7_out, and_5_out, not_2_out);
  and and_8 (and_8_out, not_2_out, and_6_out);
  nor nor_3 (out_1, and_7_out, nor_4_out);
  nor nor_4 (nor_4_out, out_1, and_8_out);

  // Notes on the sheet:
  //   Here
  //   or combination, logisim will be prone to the error. It works fine of built during a simulation, but upon 
  //   There is one way to kind of get it to work.
  //   Insert a OR gate 
  //   That will set the initializer
  //   This is the toggle swtich. Logisim cannot recognize the initialized state and goes into a error state. Not matter the variant 
  //   being reset or reopened, it will not work.
endmodule
