// Logisim project lab4_prob1a.circ as structural Verilog: 2 circuits, main circuit main
module main (
  input  in_1,
  input  [3:0] in_2,
  input  [3:0] in_3,
  input  in_4,
  input  in_5,
  input  [3:0] in_6,
  input  [3:0] in_7,
  input  in_8,
  output [3:0] out_9,
  output [3:0] out_10
);

  wire and_1_out, and_2_out, clock_1_out, clock_2_out, decoder_1_out_5, decoder_1_out_6, decoder_1_out_7,
       decoder_1_out_8, decoder_1_out_9, decoder_1_out_10, decoder_1_out_11, decoder_1_out_12,
       decoder_1_out_13, decoder_1_out_14, decoder_1_out_15, decoder_1_out_16, decoder_1_out_17,
       decoder_1_out_18, decoder_1_out_19, decoder_2_out_5, decoder_2_out_6, decoder_2_out_7,
       decoder_2_out_8, decoder_2_out_9, decoder_2_out_10, decoder_2_out_11, decoder_2_out_12,
       decoder_2_out_13, decoder_2_out_14, decoder_2_out_15, decoder_2_out_16, decoder_2_out_17,
       decoder_2_out_18, decoder_2_out_19, xor_1_out;
  wire [3:0] adder_1_out, multiplexer_1_out, multiplexer_2_out, subtractor_1_out;

  xor xor_1 (xor_1_out, in_4, in_8);
  Multiplexer #(.width(4)) multiplexer_1 (
    .in0(in_3), .in1(subtractor_1_out), .out(multiplexer_1_out), .sel(and_1_out));  // open: en
  and and_1 (and_1_out, in_4, xor_1_out);
  Multiplexer #(.width(4)) multiplexer_2 (
    .in0(in_7), .in1(adder_1_out), .out(multiplexer_2_out), .sel(and_2_out));  // open: en
  and and_2 (and_2_out, xor_1_out, in_8);
  Subtractor #(.width(4)) subtractor_1 (.a(out_9), .b(in_2), .out(subtractor_1_out), .bin(in_1));  // open: bout
  Register #(.width(4)) register_1 (.D(multiplexer_1_out), .Q(out_9), .clk(clock_1_out));  // open: en, clr
  Clock clock_1 (.out(clock_1_out));
  Adder #(.width(4)) adder_1 (.a(in_6), .b(out_10), .out(adder_1_out), .cin(in_5));  // open: cout
  Register #(.width(4)) register_2 (.D(multiplexer_2_out), .Q(out_10), .clk(clock_2_out));  // open: en, clr
  Clock clock_2 (.out(clock_2_out));
  Decoder decoder_1 (
    .in_1(out_10[0]), .in_2(out_10[1]), .in_3(out_10[2]), .in_4(out_10[3]), .out_5(decoder_1_out_5),
    .out_6(decoder_1_out_6), .out_7(decoder_1_out_7), .out_8(decoder_1_out_8), .out_9(decoder_1_out_9),
    .out_10(decoder_1_out_10), .out_11(decoder_1_out_11), .out_12(decoder_1_out_12),
    .out_13(decoder_1_out_13), .out_14(decoder_1_out_14), .out_15(decoder_1_out_15),
    .out_16(decoder_1_out_16), .out_17(decoder_1_out_17), .out_18(decoder_1_out_18), .out_19(decoder_1_out_19));
  Decoder decoder_2 (
    .in_1(out_9[0]), .in_2(out_9[1]), .in_3(out_9[2]), .in_4(out_9[3]), .out_5(decoder_2_out_5),
    .out_6(decoder_2_out_6), .out_7(decoder_2_out_7), .out_8(decoder_2_out_8), .out_9(decoder_2_out_9),
    .out_10(decoder_2_out_10), .out_11(decoder_2_out_11), .out_12(decoder_2_out_12),
    .out_13(decoder_2_out_13), .out_14(decoder_2_out_14), .out_15(decoder_2_out_15),
    .out_16(decoder_2_out_16), .out_17(decoder_2_out_17), .out_18(decoder_2_out_18), .out_19(decoder_2_out_19));
  LED led_1 (.in(decoder_2_out_5));
  LED led_2 (.in(decoder_2_out_6));
  LED led_3 (.in(decoder_2_out_7));
  LED led_4 (.in(decoder_2_out_8));
  LED led_5 (.in(decoder_2_out_9));
  LED led_6 (.in(decoder_2_out_10));
  LED led_7 (.in(decoder_2_out_11));
  LED led_8 (.in(decoder_2_out_12));
  LED led_9 (.in(decoder_2_out_13));
  LED led_10 (.in(decoder_2_out_14));
  LED led_11 (.in(decoder_2_out_15));
  LED led_12 (.in(decoder_2_out_16));
  LED led_13 (.in(decoder_2_out_17));
  LED led_14 (.in(decoder_2_out_18));
  LED led_15 (.in(decoder_2_out_19));
  LED led_16 (.in(decoder_1_out_5));
  LED led_17 (.in(decoder_1_out_6));
  LED led_18 (.in(decoder_1_out_7));
  LED led_19 (.in(decoder_1_out_8));
  LED led_20 (.in(decoder_1_out_9));
  LED led_21 (.in(decoder_1_out_10));
  LED led_22 (.in(decoder_1_out_11));
  LED led_23 (.in(decoder_1_out_12));
  LED led_24 (.in(decoder_1_out_13));
  LED led_25 (.in(decoder_1_out_14));
  LED led_26 (.in(decoder_1_out_15));
  LED led_27 (.in(decoder_1_out_16));
  LED led_28 (.in(decoder_1_out_17));
  LED led_29 (.in(decoder_1_out_18));
  LED led_30 (.in(decoder_1_out_19));
endmodule

module Decoder (
  input  in_1,
  input  in_2,
  input  in_3,
  input  in_4,
  output out_5,
  output out_6,
  output out_7,
  output out_8,
  output out_9,
  output out_10,
  output out_11,
  output out_12,
  output out_13,
  output out_14,
  output out_15,
  output out_16,
  output out_17,
  output out_18,
  output out_19
);

  wire not_1_out, not_2_out, not_3_out, not_4_out, not_5_out, not_6_out, not_7_out, not_8_out, not_9_out,
       not_10_out, not_11_out, not_12_out, not_13_out, not_14_out, not_15_out, not_16_out, not_17_out,
       not_18_out, not_19_out, not_20_out, not_21_out, not_22_out, not_23_out, not_24_out, not_25_out,
       not_26_out, not_27_out, not_28_out;

  not not_1 (not_1_out, in_2);
  not not_2 (not_2_out, in_3);
  not not_3 (not_3_out, in_4);
  not not_4 (not_4_out, in_1);
  not not_5 (not_5_out, in_3);
  not not_6 (not_6_out, in_4);
  not not_7 (not_7_out, in_3);
  not not_8 (not_8_out, in_4);
  not not_9 (not_9_out, in_1);
  not not_10 (not_10_out, in_2);
  not not_11 (not_11_out, in_4);
  not not_12 (not_12_out, in_2);
  not not_13 (not_13_out, in_4);
  not not_14 (not_14_out, in_1);
  not not_15 (not_15_out, in_4);
  not not_16 (not_16_out, in_4);
  not not_17 (not_17_out, in_1);
  not not_18 (not_18_out, in_2);
  not not_19 (not_19_out, in_3);
  not not_20 (not_20_out, in_2);
  not not_21 (not_21_out, in_3);
  not not_22 (not_22_out, in_1);
  not not_23 (not_23_out, in_3);
  not not_24 (not_24_out, in_3);
  not not_25 (not_25_out, in_1);
  not not_26 (not_26_out, in_2);
  not not_27 (not_27_out, in_2);
  not not_28 (not_28_out, in_1);
  and and_1 (out_5, in_1, not_1_out, not_2_out, not_3_out);
  and and_2 (out_6, not_4_out, in_2, not_5_out, not_6_out);
  and and_3 (out_7, in_1, in_2, not_7_out, not_8_out);
  and and_4 (out_8, not_9_out, not_10_out, in_3, not_11_out);
  and and_5 (out_9, in_1, not_12_out, in_3, not_13_out);
  and and_6 (out_10, not_14_out, in_2, in_3, not_15_out);
  and and_7 (out_11, in_1, in_2, in_3, not_16_out);
  and and_8 (out_12, not_17_out, not_18_out, not_19_out, in_4);
  and and_9 (out_13, in_1, not_20_out, not_21_out, in_4);
  and and_10 (out_14, not_22_out, in_2, not_23_out, in_4);
  and and_11 (out_15, in_1, in_2, not_24_out, in_4);
  and and_12 (out_16, not_25_out, not_26_out, in_3, in_4);
  and and_13 (out_17, in_1, not_27_out, in_3, in_4);
  and and_14 (out_18, not_28_out, in_2, in_3, in_4);
  and and_15 (out_19, in_1, in_2, in_3, in_4);
endmodule
