// Logisim project lab4_prob1aPrototype.circ as structural Verilog: 3 circuits, main circuit main
module main (
  input  in_1,
  input  [7:0] in_2,
  input  [7:0] in_3,
  input  in_4,
  input  in_5,
  input  [3:0] in_6,
  input  [3:0] in_7,
  input  in_8,
  output [7:0] out_9,
  output out_10,
  output out_11,
  output out_12,
  output out_13
);

  wire and_1_out, and_2_out, and_3_out, and_4_out, and_5_out, and_6_out, and_7_out, and_8_out, and_9_out,
       and_10_out, and_11_out, and_12_out, and_13_out, and_14_out, and_15_out, clock_1_out, clock_2_out,
       not_1_out, not_2_out, not_3_out, not_4_out, not_5_out, not_6_out, not_7_out, not_8_out, not_9_out,
       not_10_out, not_11_out, not_12_out, not_13_out, not_14_out, not_15_out, not_16_out, not_17_out,
       not_18_out, not_19_out, not_20_out, not_21_out, not_22_out, not_23_out, not_24_out, not_25_out,
       not_26_out, not_27_out, not_28_out, or_1_out;
  wire [3:0] multiplexer_1_out, subtractor_1_out;
  wire [7:0] adder_1_out, multiplexer_2_out;

  Subtractor #(.width(4)) subtractor_1 (
    .a({out_13, out_12, out_11, out_10}), .b(in_7), .out(subtractor_1_out), .bin(in_5));  // open: bout
  Multiplexer #(.width(4)) multiplexer_1 (
    .in0(in_6), .in1(subtractor_1_out), .out(multiplexer_1_out), .sel(in_8));  // open: en
  Clock clock_1 (.out(clock_1_out));
  Register register_1 ();  // open: D, en, Q, clk, clr
  or or_1 (or_1_out, multiplexer_1_out[0], multiplexer_1_out[1], multiplexer_1_out[2], multiplexer_1_out[3]);
  LED led_1 (.in(and_1_out));
  and and_1 (and_1_out, out_13, out_12, out_11, out_10);
  J_K_Flip_Flop j_k_ff_1 (.J(or_1_out), .clk(clock_1_out), .K(or_1_out), .Q(out_10));  // open: Qn, preset, en, reset
  not not_1 (not_1_out, out_10);
  LED led_2 (.in(and_2_out));
  and and_2 (and_2_out, out_13, out_12, out_11, not_1_out);
  not not_2 (not_2_out, out_11);
  and and_3 (and_3_out, out_13, out_12, not_2_out, out_10);
  LED led_3 (.in(and_3_out));
  not not_3 (not_3_out, out_10);
  not not_4 (not_4_out, out_12);
  not not_5 (not_5_out, out_11);
  LED led_4 (.in(and_5_out));
  LED led_5 (.in(and_4_out));
  and and_4 (and_4_out, out_13, out_12, not_5_out, not_3_out);
  and and_5 (and_5_out, out_13, not_4_out, out_11, out_10);
  not not_6 (not_6_out, out_12);
  LED led_6 (.in(and_6_out));
  and and_6 (and_6_out, out_13, not_6_out, out_11, not_7_out);
  J_K_Flip_Flop j_k_ff_2 (.J(or_1_out), .clk(out_10), .K(or_1_out), .Q(out_11));  // open: Qn, preset, en, reset
  not not_7 (not_7_out, out_10);
  not not_8 (not_8_out, out_11);
  not not_9 (not_9_out, out_12);
  and and_7 (and_7_out, out_13, not_9_out, not_8_out, out_10);
  LED led_7 (.in(and_7_out));
  not not_10 (not_10_out, out_12);
  not not_11 (not_11_out, out_10);
  not not_12 (not_12_out, out_11);
  and and_8 (and_8_out, out_13, not_10_out, not_12_out, not_11_out);
  LED led_8 (.in(and_8_out));
  Multiplexer #(.width(8)) multiplexer_2 (
    .in0(in_3), .in1(adder_1_out), .out(multiplexer_2_out), .sel(in_4));  // open: en
  not not_13 (not_13_out, out_13);
  and and_9 (and_9_out, not_13_out, out_12, out_11, out_10);
  LED led_9 (.in(and_9_out));
  Adder adder_1 (.a(in_2), .b(out_9), .out(adder_1_out), .cin(in_1));  // open: cout
  Register register_2 (.D(multiplexer_2_out), .Q(out_9), .clk(clock_2_out));  // open: en, clr
  Clock clock_2 (.out(clock_2_out));
  not not_14 (not_14_out, out_13);
  not not_15 (not_15_out, out_10);
  not not_16 (not_16_out, out_13);
  and and_10 (and_10_out, not_16_out, out_12, out_11, not_15_out);
  LED led_10 (.in(and_10_out));
  J_K_Flip_Flop j_k_ff_3 (.J(or_1_out), .clk(out_11), .K(or_1_out), .Q(out_12));  // open: Qn, preset, en, reset
  not not_17 (not_17_out, out_13);
  not not_18 (not_18_out, out_11);
  and and_11 (and_11_out, not_14_out, out_12, not_18_out, out_10);
  LED led_11 (.in(and_11_out));
  not not_19 (not_19_out, out_10);
  not not_20 (not_20_out, out_11);
  not not_21 (not_21_out, out_12);
  not not_22 (not_22_out, out_13);
  LED led_12 (.in(and_13_out));
  LED led_13 (.in(and_12_out));
  and and_12 (and_12_out, not_22_out, not_21_out, out_11, out_10);
  and and_13 (and_13_out, not_17_out, out_12, not_20_out, not_19_out);
  not not_23 (not_23_out, out_13);
  not not_24 (not_24_out, out_12);
  and and_14 (and_14_out, not_23_out, not_24_out, out_11, not_27_out);
  LED led_14 (.in(and_14_out));
  J_K_Flip_Flop j_k_ff_4 (.J(or_1_out), .clk(out_12), .K(or_1_out), .Q(out_13));  // open: Qn, preset, en, reset
  not not_25 (not_25_out, out_11);
  not not_26 (not_26_out, out_13);
  not not_27 (not_27_out, out_10);
  not not_28 (not_28_out, out_12);
  LED led_15 (.in(and_15_out));
  and and_15 (and_15_out, not_26_out, not_28_out, not_25_out, out_10);
endmodule

module Up_Down_Counter (
  input  in_1,
  output out_2,
  output out_3,
  output out_4,
  output out_5
);

  wire and_1_out, clock_1_out;

  Clock clock_1 (.out(clock_1_out));
  D_Flip_Flop d_ff_1 (.clk(clock_1_out), .D(in_1), .Q(out_2), .reset(and_1_out));  // open: Qn, preset, en
  D_Flip_Flop d_ff_2 (.clk(clock_1_out), .D(out_2), .Q(out_3), .reset(and_1_out));  // open: Qn, preset, en
  D_Flip_Flop d_ff_3 (.clk(clock_1_out), .D(out_3), .Q(out_4), .reset(and_1_out));  // open: Qn, preset, en
  D_Flip_Flop d_ff_4 (.clk(clock_1_out), .D(out_4), .Q(out_5), .reset(and_1_out));  // open: Qn, preset, en
  and and_1 (and_1_out, out_2, out_3, out_4, out_5);
endmodule

module Counter (
  input  in_1,
  output _1,
  output _2,
  output _4,
  output _8
);

  wire clock_1_out;

  Clock clock_1 (.out(clock_1_out));
  Counter_part counter_1 ();  // open: load, D, count, Q, carry, clk, clr
  J_K_Flip_Flop j_k_ff_1 (.J(in_1), .clk(clock_1_out), .K(in_1), .Q(_1));  // open: Qn, preset, en, reset
  J_K_Flip_Flop j_k_ff_2 (.J(in_1), .clk(_1), .K(in_1), .Q(_2));  // open: Qn, preset, en, reset
  J_K_Flip_Flop j_k_ff_3 (.J(in_1), .clk(_2), .K(in_1), .Q(_4));  // open: Qn, preset, en, reset
  J_K_Flip_Flop j_k_ff_4 (.J(in_1), .clk(_4), .K(in_1), .Q(_8));  // open: Qn, preset, en, reset
endmodule
