// Logisim project lab4_prob1b.circ as structural Verilog: 1 circuit, main circuit main
module main (
  input  in_1,
  input  [3:0] in_2,
  input  [3:0] in_3,
  input  in_4,
  input  in_5,
  input  [3:0] in_6,
  input  [3:0] in_7,
  input  in_8,
  output [3:0] out_9,
  output [3:0] out_10
);

  wire and_1_out, and_2_out, clock_1_out, clock_2_out, xor_1_out;
  wire [3:0] adder_1_out, multiplexer_1_out, multiplexer_2_out, subtractor_1_out, undriven;
  wire [14:0] rom_1_data, rom_2_data, rom_3_data;

  xor xor_1 (xor_1_out, in_4, in_8);
  Multiplexer #(.width(4)) multiplexer_1 (
    .in0(in_3), .in1(subtractor_1_out), .out(multiplexer_1_out), .sel(and_1_out));  // open: en
  and and_1 (and_1_out, in_4, xor_1_out);
  Multiplexer #(.width(4)) multiplexer_2 (
    .in0(in_7), .in1(adder_1_out), .out(multiplexer_2_out), .sel(and_2_out));  // open: en
  and and_2 (and_2_out, xor_1_out, in_8);
  Subtractor #(.width(4)) subtractor_1 (.a(out_9), .b(in_2), .out(subtractor_1_out), .bin(in_1));  // open: bout
  Register #(.width(4)) register_1 (.D(multiplexer_1_out), .Q(out_9), .clk(clock_1_out));  // open: en, clr
  Clock clock_1 (.out(clock_1_out));
  Adder #(.width(4)) adder_1 (.a(in_6), .b(out_10), .out(adder_1_out), .cin(in_5));  // open: cout
  Register #(.width(4)) register_2 (.D(multiplexer_2_out), .Q(out_10), .clk(clock_2_out));  // open: en, clr
  Clock clock_2 (.out(clock_2_out));
  ROM #(.addrWidth(4), .dataWidth(15)) rom_1 (.addr(out_9), .data(rom_1_data));  // open: sel
  ROM #(.addrWidth(4), .dataWidth(15)) rom_2 (.addr(out_10), .data(rom_2_data));  // open: sel
  ROM #(.addrWidth(4), .dataWidth(15)) rom_3 (.addr(undriven), .data(rom_3_data));  // open: sel
  LED led_1 (.in(rom_3_data[14]));
  LED led_2 (.in(rom_1_data[0]));
  LED led_3 (.in(rom_1_data[1]));
  LED led_4 (.in(rom_1_data[2]));
  LED led_5 (.in(rom_1_data[3]));
  LED led_6 (.in(rom_1_data[4]));
  LED led_7 (.in(rom_1_data[5]));
  LED led_8 (.in(rom_1_data[6]));
  LED led_9 (.in(rom_1_data[7]));
  LED led_10 (.in(rom_1_data[8]));
  LED led_11 (.in(rom_1_data[9]));
  LED led_12 (.in(rom_1_data[10]));
  LED led_13 (.in(rom_1_data[11]));
  LED led_14 (.in(rom_1_data[12]));
  LED led_15 (.in(rom_1_data[13]));
  LED led_16 (.in(rom_1_data[14]));
  LED led_17 (.in(rom_2_data[0]));
  LED led_18 (.in(rom_2_data[1]));
  LED led_19 (.in(rom_2_data[2]));
  LED led_20 (.in(rom_2_data[3]));
  LED led_21 (.in(rom_2_data[4]));
  LED led_22 (.in(rom_2_data[5]));
  LED led_23 (.in(rom_2_data[6]));
  LED led_24 (.in(rom_2_data[7]));
  LED led_25 (.in(rom_2_data[8]));
  LED led_26 (.in(rom_2_data[9]));
  LED led_27 (.in(rom_2_data[10]));
  LED led_28 (.in(rom_2_data[11]));
  LED led_29 (.in(rom_2_data[12]));
  LED led_30 (.in(rom_2_data[13]));
  LED led_31 (.in(rom_2_data[14]));
  LED led_32 (.in(rom_3_data[12]));
  LED led_33 (.in(rom_3_data[11]));
  LED led_34 (.in(rom_3_data[13]));
  LED led_35 (.in(rom_3_data[9]));
  LED led_36 (.in(rom_3_data[8]));
  LED led_37 (.in(rom_3_data[10]));
  LED led_38 (.in(rom_3_data[7]));
  LED led_39 (.in(rom_3_data[6]));
  LED led_40 (.in(rom_3_data[5]));
  LED led_41 (.in(rom_3_data[4]));
  LED led_42 (.in(rom_3_data[3]));
  LED led_43 (.in(rom_3_data[0]));
  LED led_44 (.in(rom_3_data[2]));
  LED led_45 (.in(rom_3_data[1]));

  // Notes on the sheet:
  //   contents of rom_1 (hex, n*v repeats v):
  //   1 2 4 8 10 20 40 80 100 200 400 800 1000 2000 4000
  //   contents of rom_2 (hex, n*v repeats v):
  //   1 2 4 8 10 20 40 80 100 200 400 800 1000 2000 4000
  //   contents of rom_3 (hex, n*v repeats v):
  //   1 2 4 8 10 20 40 80 100 200 400 800 1000 2000 4000
endmodule
