// Logisim project lab4_prob1bPrototype.circ as structural Verilog: 1 circuit, main circuit main
module main (
  input  in_1
);

  wire clock_1_out;
  wire [3:0] j_k_ff_1_q;
  wire [14:0] rom_1_data;

  Clock clock_1 (.out(clock_1_out));
  J_K_Flip_Flop j_k_ff_1 (.J(in_1), .clk(clock_1_out), .K(in_1), .Q(j_k_ff_1_q[0]));  // open: Qn, preset, en, reset
  J_K_Flip_Flop j_k_ff_2 (.J(in_1), .clk(j_k_ff_1_q[0]), .K(in_1), .Q(j_k_ff_1_q[1]));  // open: Qn, preset, en, reset
  ROM #(.addrWidth(4), .dataWidth(15)) rom_1 (.addr(j_k_ff_1_q), .data(rom_1_data));  // open: sel
  LED led_1 (.in(rom_1_data[14]));
  J_K_Flip_Flop j_k_ff_3 (.J(in_1), .clk(j_k_ff_1_q[1]), .K(in_1), .Q(j_k_ff_1_q[2]));  // open: Qn, preset, en, reset
  LED led_2 (.in(rom_1_data[11]));
  LED led_3 (.in(rom_1_data[13]));
  LED led_4 (.in(rom_1_data[12]));
  LED led_5 (.in(rom_1_data[10]));
  LED led_6 (.in(rom_1_data[8]));
  LED led_7 (.in(rom_1_data[9]));
  LED led_8 (.in(rom_1_data[6]));
  LED led_9 (.in(rom_1_data[7]));
  LED led_10 (.in(rom_1_data[3]));
  LED led_11 (.in(rom_1_data[4]));
  LED led_12 (.in(rom_1_data[5]));
  J_K_Flip_Flop j_k_ff_4 (.J(in_1), .clk(j_k_ff_1_q[2]), .K(in_1), .Q(j_k_ff_1_q[3]));  // open: Qn, preset, en, reset
  LED led_13 (.in(rom_1_data[1]));
  LED led_14 (.in(rom_1_data[2]));
  LED led_15 (.in(rom_1_data[0]));

  // Notes on the sheet:
  //   contents of rom_1 (hex, n*v repeats v):
  //   1 2 4 8 10 20 40 80 100 200 400 800 1000 2000 4000
endmodule
