// Logisim project lab4_prob3.circ as structural Verilog
module Adder (
  input  A,
  input  B,
  input  C,
  output C0,
  output S
);

  wire and_1_out, and_2_out, and_3_out, and_4_out, and_5_out, and_6_out, and_7_out, not_1_out, not_2_out,
       not_3_out;

  or or_1 (C0, and_1_out, and_2_out, and_3_out);
  or or_2 (S, and_4_out, and_5_out, and_6_out, and_7_out);
  and and_1 (and_1_out, A, B);
  and and_2 (and_2_out, A, C);
  and and_3 (and_3_out, B, C);
  and and_4 (and_4_out, not_1_out, not_2_out, C);
  and and_5 (and_5_out, not_1_out, B, not_3_out);
  and and_6 (and_6_out, A, not_2_out, not_3_out);
  and and_7 (and_7_out, A, B, C);
  not not_1 (not_1_out, A);
  not not_2 (not_2_out, B);
  not not_3 (not_3_out, C);
endmodule

module Adder__8_bit (
  input  [7:0] Input_A,
  input  [7:0] Input_B,
  output out_3,
  output [7:0] out_4
);

  wire adder_2_c0, adder_3_c0, adder_4_c0, adder_5_c0, adder_6_c0, adder_7_c0, adder_8_c0, button_1_out;

  Adder adder_1 (.C0(out_3), .S(out_4[7]), .A(Input_A[7]), .B(Input_B[7]), .C(adder_2_c0));
  Adder adder_2 (.C0(adder_2_c0), .S(out_4[6]), .A(Input_A[6]), .B(Input_B[6]), .C(adder_3_c0));
  Adder adder_3 (.C0(adder_3_c0), .S(out_4[5]), .A(Input_A[5]), .B(Input_B[5]), .C(adder_4_c0));
  Adder adder_4 (.C0(adder_4_c0), .S(out_4[4]), .A(Input_A[4]), .B(Input_B[4]), .C(adder_5_c0));
  Adder adder_5 (.C0(adder_5_c0), .S(out_4[3]), .A(Input_A[3]), .B(Input_B[3]), .C(adder_6_c0));
  Adder adder_6 (.C0(adder_6_c0), .S(out_4[2]), .A(Input_A[2]), .B(Input_B[2]), .C(adder_7_c0));
  Adder adder_7 (.C0(adder_7_c0), .S(out_4[1]), .A(Input_A[1]), .B(Input_B[1]), .C(adder_8_c0));
  Button button_1 (.out(button_1_out));
  Adder adder_8 (.C0(adder_8_c0), .S(out_4[0]), .A(Input_A[0]), .B(Input_B[0]), .C(button_1_out));
endmodule

module Subtractor__8_bit (
  input  [7:0] Input_A,
  input  [7:0] Input_B,
  output out_3,
  output [7:0] out_4
);

  wire adder_2_c0, adder_3_c0, adder_4_c0, adder_5_c0, adder_6_c0, adder_7_c0, adder_8_c0, button_1_out,
       not_2_out;
  wire [7:0] not_1_out;

  assign not_1_out = ~Input_B;  // NOT_Gate not_1, 8 bits wide
  Adder adder_1 (.C0(out_3), .S(out_4[7]), .A(Input_A[7]), .B(not_1_out[7]), .C(adder_2_c0));
  Adder adder_2 (.C0(adder_2_c0), .S(out_4[6]), .A(Input_A[6]), .B(not_1_out[6]), .C(adder_3_c0));
  Adder adder_3 (.C0(adder_3_c0), .S(out_4[5]), .A(Input_A[5]), .B(not_1_out[5]), .C(adder_4_c0));
  Adder adder_4 (.C0(adder_4_c0), .S(out_4[4]), .A(Input_A[4]), .B(not_1_out[4]), .C(adder_5_c0));
  Adder adder_5 (.C0(adder_5_c0), .S(out_4[3]), .A(Input_A[3]), .B(not_1_out[3]), .C(adder_6_c0));
  Adder adder_6 (.C0(adder_6_c0), .S(out_4[2]), .A(Input_A[2]), .B(not_1_out[2]), .C(adder_7_c0));
  Adder adder_7 (.C0(adder_7_c0), .S(out_4[1]), .A(Input_A[1]), .B(not_1_out[1]), .C(adder_8_c0));
  Button button_1 (.out(button_1_out));
  not not_2 (not_2_out, button_1_out);
  Adder adder_8 (.C0(adder_8_c0), .S(out_4[0]), .A(Input_A[0]), .B(not_1_out[0]), .C(not_2_out));
endmodule

module Multiplexer (
  input  in_1,
  input  in_2,
  input  in_3,
  input  in_4,
  input  in_5,
  output out_6
);

  wire and_1_out, and_2_out, and_3_out, not_1_out, not_2_out;

  not not_1 (not_1_out, in_4);
  not not_2 (not_2_out, in_5);
  and and_1 (and_1_out, in_5, not_1_out, in_1);
  and and_2 (and_2_out, not_2_out, in_4, in_2);
  or or_1 (out_6, and_1_out, and_2_out, and_3_out);
  and and_3 (and_3_out, in_5, in_4, in_3);
endmodule

module Bit_Shifter__1 (
  input  [7:0] Input,
  input  Left,
  input  Clock,
  input  Right,
  output [7:0] Output
);

  wire button_1_out, button_2_out, multiplexer_1_out_6, multiplexer_2_out_6, multiplexer_3_out_6,
       multiplexer_4_out_6, multiplexer_5_out_6, multiplexer_6_out_6, multiplexer_7_out_6,
       multiplexer_8_out_6, not_1_out, or_1_out, xor_1_out;

  xor xor_1 (xor_1_out, Left, Right);
  not not_1 (not_1_out, Right);
  or or_1 (or_1_out, not_1_out, xor_1_out);
  Button button_1 (.out(button_1_out));
  Multiplexer multiplexer_1 (
    .in_4(xor_1_out), .in_5(not_1_out), .in_1(Input[7]), .in_2(button_1_out), .in_3(Output[6]),
    .out_6(multiplexer_1_out_6));
  Multiplexer multiplexer_2 (
    .in_4(xor_1_out), .in_5(not_1_out), .in_1(Input[6]), .in_2(Output[7]), .in_3(Output[5]),
    .out_6(multiplexer_2_out_6));
  Register #(.width(1)) register_1 (.D(multiplexer_1_out_6), .en(or_1_out), .Q(Output[7]), .clk(Clock));  // open: clr
  Register #(.width(1)) register_2 (.D(multiplexer_2_out_6), .en(or_1_out), .Q(Output[6]), .clk(Clock));  // open: clr
  Multiplexer multiplexer_3 (
    .in_4(xor_1_out), .in_5(not_1_out), .in_1(Input[5]), .in_2(Output[6]), .in_3(Output[4]),
    .out_6(multiplexer_3_out_6));
  Register #(.width(1)) register_3 (.D(multiplexer_3_out_6), .en(or_1_out), .Q(Output[5]), .clk(Clock));  // open: clr
  Multiplexer multiplexer_4 (
    .in_4(xor_1_out), .in_5(not_1_out), .in_1(Input[4]), .in_2(Output[5]), .in_3(Output[3]),
    .out_6(multiplexer_4_out_6));
  Register #(.width(1)) register_4 (.D(multiplexer_4_out_6), .en(or_1_out), .Q(Output[4]), .clk(Clock));  // open: clr
  Multiplexer multiplexer_5 (
    .in_4(xor_1_out), .in_5(not_1_out), .in_1(Input[3]), .in_2(Output[4]), .in_3(Output[2]),
    .out_6(multiplexer_5_out_6));
  Multiplexer multiplexer_6 (
    .in_4(xor_1_out), .in_5(not_1_out), .in_1(Input[2]), .in_2(Output[3]), .in_3(Output[1]),
    .out_6(multiplexer_6_out_6));
  Register #(.width(1)) register_5 (.D(multiplexer_5_out_6), .en(or_1_out), .Q(Output[3]), .clk(Clock));  // open: clr
  Register #(.width(1)) register_6 (.D(multiplexer_6_out_6), .en(or_1_out), .Q(Output[2]), .clk(Clock));  // open: clr
  Multiplexer multiplexer_7 (
    .in_4(xor_1_out), .in_5(not_1_out), .in_1(Input[1]), .in_2(Output[2]), .in_3(Output[0]),
    .out_6(multiplexer_7_out_6));
  Register #(.width(1)) register_7 (.D(multiplexer_7_out_6), .en(or_1_out), .Q(Output[1]), .clk(Clock));  // open: clr
  Multiplexer multiplexer_8 (
    .in_4(xor_1_out), .in_5(not_1_out), .in_1(Input[0]), .in_2(Output[1]), .in_3(button_2_out),
    .out_6(multiplexer_8_out_6));
  Register #(.width(1)) register_8 (.D(multiplexer_8_out_6), .en(or_1_out), .Q(Output[0]), .clk(Clock));  // open: clr
  Button button_2 (.out(button_2_out));
endmodule

module Bit_Shifter__2 (
  input  [7:0] Input,
  input  Left,
  input  Clock,
  input  Right,
  output [7:0] Output
);

  wire button_1_out, button_2_out, multiplexer_1_out_6, multiplexer_2_out_6, multiplexer_3_out_6,
       multiplexer_4_out_6, multiplexer_5_out_6, multiplexer_6_out_6, multiplexer_7_out_6,
       multiplexer_8_out_6, not_1_out, or_1_out, xor_1_out;

  xor xor_1 (xor_1_out, Left, Right);
  not not_1 (not_1_out, Right);
  or or_1 (or_1_out, not_1_out, xor_1_out);
  Button button_1 (.out(button_1_out));
  Multiplexer multiplexer_1 (
    .in_4(xor_1_out), .in_5(not_1_out), .in_1(Input[7]), .in_2(button_1_out), .in_3(Output[5]),
    .out_6(multiplexer_1_out_6));
  Multiplexer multiplexer_2 (
    .in_4(xor_1_out), .in_5(not_1_out), .in_1(Input[6]), .in_2(button_1_out), .in_3(Output[4]),
    .out_6(multiplexer_2_out_6));
  Register #(.width(1)) register_1 (.D(multiplexer_1_out_6), .en(or_1_out), .Q(Output[7]), .clk(Clock));  // open: clr
  Register #(.width(1)) register_2 (.D(multiplexer_2_out_6), .en(or_1_out), .Q(Output[6]), .clk(Clock));  // open: clr
  Multiplexer multiplexer_3 (
    .in_4(xor_1_out), .in_5(not_1_out), .in_1(Input[5]), .in_2(Output[7]), .in_3(Output[3]),
    .out_6(multiplexer_3_out_6));
  Register #(.width(1)) register_3 (.D(multiplexer_3_out_6), .en(or_1_out), .Q(Output[5]), .clk(Clock));  // open: clr
  Multiplexer multiplexer_4 (
    .in_4(xor_1_out), .in_5(not_1_out), .in_1(Input[4]), .in_2(Output[6]), .in_3(Output[2]),
    .out_6(multiplexer_4_out_6));
  Register #(.width(1)) register_4 (.D(multiplexer_4_out_6), .en(or_1_out), .Q(Output[4]), .clk(Clock));  // open: clr
  Multiplexer multiplexer_5 (
    .in_4(xor_1_out), .in_5(not_1_out), .in_1(Input[3]), .in_2(Output[5]), .in_3(Output[1]),
    .out_6(multiplexer_5_out_6));
  Multiplexer multiplexer_6 (
    .in_4(xor_1_out), .in_5(not_1_out), .in_1(Input[2]), .in_2(Output[4]), .in_3(Output[0]),
    .out_6(multiplexer_6_out_6));
  Register #(.width(1)) register_5 (.D(multiplexer_5_out_6), .en(or_1_out), .Q(Output[3]), .clk(Clock));  // open: clr
  Register #(.width(1)) register_6 (.D(multiplexer_6_out_6), .en(or_1_out), .Q(Output[2]), .clk(Clock));  // open: clr
  Multiplexer multiplexer_7 (
    .in_4(xor_1_out), .in_5(not_1_out), .in_1(Input[1]), .in_2(button_2_out), .in_3(Output[3]),
    .out_6(multiplexer_7_out_6));
  Register #(.width(1)) register_7 (.D(multiplexer_7_out_6), .en(or_1_out), .Q(Output[1]), .clk(Clock));  // open: clr
  Multiplexer multiplexer_8 (
    .in_4(xor_1_out), .in_5(not_1_out), .in_1(Input[0]), .in_2(Output[2]), .in_3(button_2_out),
    .out_6(multiplexer_8_out_6));
  Register #(.width(1)) register_8 (.D(multiplexer_8_out_6), .en(or_1_out), .Q(Output[0]), .clk(Clock));  // open: clr
  Button button_2 (.out(button_2_out));
endmodule

module Bit_Shifter__4 (
  input  [7:0] Input,
  input  Left,
  input  Clock,
  input  Right,
  output [7:0] Output
);

  wire button_1_out, button_2_out, multiplexer_1_out_6, multiplexer_2_out_6, multiplexer_3_out_6,
       multiplexer_4_out_6, multiplexer_5_out_6, multiplexer_6_out_6, multiplexer_7_out_6,
       multiplexer_8_out_6, not_1_out, or_1_out, xor_1_out;

  xor xor_1 (xor_1_out, Left, Right);
  not not_1 (not_1_out, Right);
  or or_1 (or_1_out, not_1_out, xor_1_out);
  Button button_1 (.out(button_1_out));
  Multiplexer multiplexer_1 (
    .in_4(xor_1_out), .in_5(not_1_out), .in_1(Input[7]), .in_2(button_1_out), .in_3(Output[3]),
    .out_6(multiplexer_1_out_6));
  Multiplexer multiplexer_2 (
    .in_4(xor_1_out), .in_5(not_1_out), .in_1(Input[6]), .in_2(button_1_out), .in_3(Output[2]),
    .out_6(multiplexer_2_out_6));
  Register #(.width(1)) register_1 (.D(multiplexer_1_out_6), .en(or_1_out), .Q(Output[7]), .clk(Clock));  // open: clr
  Register #(.width(1)) register_2 (.D(multiplexer_2_out_6), .en(or_1_out), .Q(Output[6]), .clk(Clock));  // open: clr
  Multiplexer multiplexer_3 (
    .in_4(xor_1_out), .in_5(not_1_out), .in_1(Input[5]), .in_2(button_1_out), .in_3(Output[1]),
    .out_6(multiplexer_3_out_6));
  Register #(.width(1)) register_3 (.D(multiplexer_3_out_6), .en(or_1_out), .Q(Output[5]), .clk(Clock));  // open: clr
  Multiplexer multiplexer_4 (
    .in_4(xor_1_out), .in_5(not_1_out), .in_1(Input[4]), .in_2(button_1_out), .in_3(Output[0]),
    .out_6(multiplexer_4_out_6));
  Register #(.width(1)) register_4 (.D(multiplexer_4_out_6), .en(or_1_out), .Q(Output[4]), .clk(Clock));  // open: clr
  Multiplexer multiplexer_5 (
    .in_4(xor_1_out), .in_5(not_1_out), .in_1(Input[3]), .in_2(Output[7]), .in_3(button_2_out),
    .out_6(multiplexer_5_out_6));
  Multiplexer multiplexer_6 (
    .in_4(xor_1_out), .in_5(not_1_out), .in_1(Input[2]), .in_2(Output[6]), .in_3(button_2_out),
    .out_6(multiplexer_6_out_6));
  Register #(.width(1)) register_5 (.D(multiplexer_5_out_6), .en(or_1_out), .Q(Output[3]), .clk(Clock));  // open: clr
  Register #(.width(1)) register_6 (.D(multiplexer_6_out_6), .en(or_1_out), .Q(Output[2]), .clk(Clock));  // open: clr
  Multiplexer multiplexer_7 (
    .in_4(xor_1_out), .in_5(not_1_out), .in_1(Input[1]), .in_2(Output[5]), .in_3(button_2_out),
    .out_6(multiplexer_7_out_6));
  Register #(.width(1)) register_7 (.D(multiplexer_7_out_6), .en(or_1_out), .Q(Output[1]), .clk(Clock));  // open: clr
  Multiplexer multiplexer_8 (
    .in_4(xor_1_out), .in_5(not_1_out), .in_1(Input[0]), .in_2(Output[4]), .in_3(button_2_out),
    .out_6(multiplexer_8_out_6));
  Register #(.width(1)) register_8 (.D(multiplexer_8_out_6), .en(or_1_out), .Q(Output[0]), .clk(Clock));  // open: clr
  Button button_2 (.out(button_2_out));
endmodule

module Magnitude_Comparator (
  input  a,
  input  b,
  input  Previously_Greater,
  input  Previously_Equal,
  input  Previously_Less,
  output A___B,
  output A____B,
  output A___B_2
);

  wire and_1_out, and_2_out, and_3_out, and_4_out, not_1_out, not_2_out;

  not not_1 (not_1_out, a);
  not not_2 (not_2_out, b);
  and and_1 (and_1_out, not_2_out, Previously_Equal, a);
  and and_2 (and_2_out, b, Previously_Equal, a);
  or or_1 (A____B, and_2_out, and_3_out);
  and and_3 (and_3_out, not_2_out, Previously_Equal, not_1_out);
  and and_4 (and_4_out, b, Previously_Equal, not_1_out);
  or or_2 (A___B, Previously_Greater, and_1_out);
  or or_3 (A___B_2, and_4_out, Previously_Less);
endmodule

module Magnitude_Comparator__8_bit (
  input  [7:0] A,
  input  [7:0] B,
  output A___B,
  output A____B,
  output A___B_2
);

  wire button_1_out, button_2_out, button_3_out, magnitude_comparator_1_a____b, magnitude_comparator_1_a___b,
       magnitude_comparator_1_a___b_2, magnitude_comparator_2_a____b, magnitude_comparator_2_a___b,
       magnitude_comparator_2_a___b_2, magnitude_comparator_3_a____b, magnitude_comparator_3_a___b,
       magnitude_comparator_3_a___b_2, magnitude_comparator_4_a____b, magnitude_comparator_4_a___b,
       magnitude_comparator_4_a___b_2, magnitude_comparator_5_a____b, magnitude_comparator_5_a___b,
       magnitude_comparator_5_a___b_2, magnitude_comparator_6_a____b, magnitude_comparator_6_a___b,
       magnitude_comparator_6_a___b_2, magnitude_comparator_7_a____b, magnitude_comparator_7_a___b,
       magnitude_comparator_7_a___b_2, not_1_out;

  Button button_1 (.out(button_1_out));
  Button button_2 (.out(button_2_out));
  Button button_3 (.out(button_3_out));
  Magnitude_Comparator magnitude_comparator_1 (
    .a(A[7]), .b(B[7]), .A___B(magnitude_comparator_1_a___b), .Previously_Greater(button_1_out),
    .Previously_Equal(not_1_out), .A____B(magnitude_comparator_1_a____b), .Previously_Less(button_3_out),
    .A___B_2(magnitude_comparator_1_a___b_2));
  not not_1 (not_1_out, button_2_out);
  Magnitude_Comparator magnitude_comparator_2 (
    .a(A[6]), .b(B[6]), .A___B(magnitude_comparator_2_a___b),
    .Previously_Greater(magnitude_comparator_1_a___b), .Previously_Equal(magnitude_comparator_1_a____b),
    .A____B(magnitude_comparator_2_a____b), .Previously_Less(magnitude_comparator_1_a___b_2),
    .A___B_2(magnitude_comparator_2_a___b_2));
  Magnitude_Comparator magnitude_comparator_3 (
    .a(A[5]), .b(B[5]), .A___B(magnitude_comparator_3_a___b),
    .Previously_Greater(magnitude_comparator_2_a___b), .Previously_Equal(magnitude_comparator_2_a____b),
    .A____B(magnitude_comparator_3_a____b), .Previously_Less(magnitude_comparator_2_a___b_2),
    .A___B_2(magnitude_comparator_3_a___b_2));
  Magnitude_Comparator magnitude_comparator_4 (
    .a(A[4]), .b(B[4]), .A___B(magnitude_comparator_4_a___b),
    .Previously_Greater(magnitude_comparator_3_a___b), .Previously_Equal(magnitude_comparator_3_a____b),
    .A____B(magnitude_comparator_4_a____b), .Previously_Less(magnitude_comparator_3_a___b_2),
    .A___B_2(magnitude_comparator_4_a___b_2));
  Magnitude_Comparator magnitude_comparator_5 (
    .a(A[3]), .b(B[3]), .A___B(magnitude_comparator_5_a___b),
    .Previously_Greater(magnitude_comparator_4_a___b), .Previously_Equal(magnitude_comparator_4_a____b),
    .A____B(magnitude_comparator_5_a____b), .Previously_Less(magnitude_comparator_4_a___b_2),
    .A___B_2(magnitude_comparator_5_a___b_2));
  Magnitude_Comparator magnitude_comparator_6 (
    .a(A[2]), .b(B[2]), .A___B(magnitude_comparator_6_a___b),
    .Previously_Greater(magnitude_comparator_5_a___b), .Previously_Equal(magnitude_comparator_5_a____b),
    .A____B(magnitude_comparator_6_a____b), .Previously_Less(magnitude_comparator_5_a___b_2),
    .A___B_2(magnitude_comparator_6_a___b_2));
  Magnitude_Comparator magnitude_comparator_7 (
    .a(A[1]), .b(B[1]), .A___B(magnitude_comparator_7_a___b),
    .Previously_Greater(magnitude_comparator_6_a___b), .Previously_Equal(magnitude_comparator_6_a____b),
    .A____B(magnitude_comparator_7_a____b), .Previously_Less(magnitude_comparator_6_a___b_2),
    .A___B_2(magnitude_comparator_7_a___b_2));
  Magnitude_Comparator magnitude_comparator_8 (
    .a(A[0]), .b(B[0]), .A___B(A___B), .Previously_Greater(magnitude_comparator_7_a___b),
    .Previously_Equal(magnitude_comparator_7_a____b), .A____B(A____B),
    .Previously_Less(magnitude_comparator_7_a___b_2), .A___B_2(A___B_2));
endmodule

module Barrel_Shifter (
  input  [7:0] Input,
  input  Right___1__Left___0,
  input  [2:0] Shift_Bits,
  output [7:0] out_4,
  output [7:0] out_5,
  output [7:0] out_6
);

  wire and_1_out, and_2_out, and_3_out, and_4_out, and_5_out, and_6_out, clock_1_out, not_1_out;

  Clock clock_1 (.out(clock_1_out));
  not not_1 (not_1_out, Right___1__Left___0);
  and and_1 (and_1_out, Shift_Bits[2], not_1_out);
  and and_2 (and_2_out, Shift_Bits[2], Right___1__Left___0);
  and and_3 (and_3_out, Shift_Bits[1], not_1_out);
  and and_4 (and_4_out, Shift_Bits[1], Right___1__Left___0);
  and and_5 (and_5_out, Shift_Bits[0], not_1_out);
  and and_6 (and_6_out, Shift_Bits[0], Right___1__Left___0);
  Bit_Shifter__4 bit_shifter_4_1 (
    .Input(Input), .Left(and_1_out), .Clock(clock_1_out), .Right(and_2_out), .Output(out_4));
  Bit_Shifter__2 bit_shifter_2_1 (
    .Input(out_4), .Left(and_3_out), .Clock(clock_1_out), .Right(and_4_out), .Output(out_5));
  Bit_Shifter__1 bit_shifter_1_1 (
    .Input(out_5), .Left(and_5_out), .Right(and_6_out), .Output(out_6), .Clock(clock_1_out));
endmodule
